// Logisim project Clock-Divider.circ as structural Verilog: 3 circuits, main circuit S-R Latch
module S_R_Latch (
  input  R,
  input  S,
  output Q,
  output Not_Q
);

  nor nor_1 (Q, R, Not_Q);
  nor nor_2 (Not_Q, Q, S);
endmodule

module D_Latch (
  input  C,
  input  D,
  output Q,
  output Not_Q
);

  wire and_1_out, and_2_out;

  and and_1 (and_1_out, C, ~D);  // AND_Gate
  and and_2 (and_2_out, C, D);
  S_R_Latch s_r_latch_1 (.R(and_1_out), .S(and_2_out), .Q(Q), .Not_Q(Not_Q));
endmodule

module D_flip_flop (
  input  D,
  output out_2,
  output out_3
);

  wire clock_1_out, d_latch_1_q, not_1_out;

  Clock clock_1 (.out(clock_1_out));
  not not_1 (not_1_out, clock_1_out);
  D_Latch d_latch_1 (.C(clock_1_out), .D(out_3), .Q(d_latch_1_q));  // open: Not_Q
  D_Latch d_latch_2 (.C(not_1_out), .D(d_latch_1_q), .Q(out_2), .Not_Q(out_3));
endmodule
